# Fritzing sketch project schematic (saved by Fritzing 0.9.3b)
breadboards: 1

parts:
  Part1 = Photon
  Part2 = HX711 Weighing Sensor Module
  Tare = Pushbutton [package="[THT]"]
  R1 = Resistor [tolerance=±5% resistance=220 package="2512 [SMD]"]
  R2 = Resistor [tolerance=±5% resistance=220 package="2512 [SMD]"]
  Start = Pushbutton [package="[THT]"]
  Part3 = Adafruit NeoParticle Ring [part_number="Adafruit #2268"]

nets:
  GND: Part1.GND, Part2.GND, Tare.Pin_4, Start.Pin_1, Start.Pin_2, Part3.GND
  VIN: Part1.VIN, Part2.VCC, R1.Pin_1, R2.Pin_0, Part3.VDD
  N1: Part1.D0, Part2.CK/TX
  N2: Part1.D1, Part2.DO/RX
  N3: Part1.D2, Part3.DIN
  N4: Part1.D3, R2.Pin_1, Start.Pin_3, Start.Pin_4
  N5: Part1.D4, Tare.Pin_1, Tare.Pin_2, R1.Pin_0

custom parts:
  Adafruit NeoParticle Ring: Add some dazzle to your Spark Core or Photon with this custom-made NeoPixel ring kit! 24 ultra bright smart LED NeoPixels are arranged in a circle with 2.6" (66mm) outer diameter. Snap in your Spark and upload the NeoPixel library code to light up the LEDs, make an Internet of Blinky! Each LED is addressable as the driver chip is inside the LED. Each one has ~18mA constant current drive so the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
