# Fritzing sketch project (saved by Fritzing 0.9.3b)
breadboards: 1

parts:
  Part2 = Photon  # not connected
  Part1 = HX711 Weighing Sensor Module
  R2 = Resistor [tolerance=±5% resistance=220 package="0603 [SMD]"]
  S1 = Pushbutton [package="[THT]"]
  S2 = Pushbutton [package="[THT]"]
  R1 = Resistor [tolerance=±5% resistance=220 package="0603 [SMD]"]
  Part3 = Adafruit NeoParticle Ring [part_number="Adafruit #2268"]

nets:
  VCC: Part1.VCC, R2.Pin_1, R1.Pin_0, Part3.VDD
  GND: Part1.GND, S1.Pin_3, S1.Pin_4, S2.Pin_3, S2.Pin_4, R1.Pin_1, Part3.GND
  N1: R2.Pin_0, S1.Pin_1, S1.Pin_2
  N2: S2.Pin_1, S2.Pin_2

notes:
  E+ (red)
  E- (black)
  A- (white)
  A+ (white)

custom parts:
  Adafruit NeoParticle Ring: Add some dazzle to your Spark Core or Photon with this custom-made NeoPixel ring kit! 24 ultra bright smart LED NeoPixels are arranged in a circle with 2.6" (66mm) outer diameter. Snap in your Spark and upload the NeoPixel library code to light up the LEDs, make an Internet of Blinky! Each LED is addressable as the driver chip is inside the LED. Each one has ~18mA constant current drive so the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
